// Logisim project ex2.circ as structural Verilog: 1 circuit, main circuit AddMachine
module AddMachine (
  output [7:0] ADD_OUT,
  output [7:0] REG_OUT
);

  Adder adder_1 (.a(REG_OUT), .b(8'h1), .out(ADD_OUT));  // open: cin, cout
  Register register_1 (.D(ADD_OUT), .Q(REG_OUT));  // open: en, clk, clr
  Clock clock_1 ();  // open: out

  // Notes on the sheet:
  //   PUT CIRCUITRY HERE
endmodule
